# Fritzing sketch Microcontrollers_Schaltung (saved by Fritzing 0.9.10b)

parts:
  Bauteil1 = Arduino Uno (Rev3)
  S1 = Pushbutton [package="[THT]"]
  S2 = Pushbutton [package="[THT]"]
  S3 = Pushbutton [package="[THT]"]
  S4 = Pushbutton [package="[THT]"]
  S5 = Pushbutton [package="[THT]"]
  IC1 = 25LC512 [package=THT]
  RHT1 = Humidity and Temperature Sensor RHT03
  Chirp!_Soil_Moisture_Sensor1 = Chirp! Soil Moisture Sensor v2.7.3
  Bauteil2 = LCD1602-I2C
  BAT1 = BC9VPC [package=bc9vpc]
  R1 = Resistor [tolerance=±5% resistance=220 package="1206 [SMD]"]  # not connected
  R2 = Resistor [tolerance=±5% resistance=220 package="1206 [SMD]"]

nets:
  N1: Bauteil1.A0, Chirp!_Soil_Moisture_Sensor1.pin_3
  N2: Bauteil1.A3, R2.Pin_1
  N3: Bauteil1.D8, S1.Pin_4
  N4: Bauteil1.D9_PWM, S4.Pin_4
  N5: Bauteil1.D10_PWM/SS, IC1.SO_-_Data_Out
  N6: Bauteil1.D12/MISO, IC1.SI_-_Data_In
  N7: Bauteil1.D13/SCK, IC1.SCK_-_SPI_Clock
  GND: Bauteil1.GND, Bauteil2.GND, BAT1.V-
  N8: Bauteil1.A4/SDA, Bauteil2.SDA
  N9: Bauteil1.A5/SCL, Bauteil2.SCL
  N10: Bauteil1.D0/RX, S2.Pin_4
  N11: Bauteil1.D2, RHT1.Data-signal
  N12: Bauteil1.D4, S5.Pin_4
  N13: Bauteil1.D6_PWM, S3.Pin_4
  N14: Bauteil1.D7, IC1.CS_-_Chip_Select
  5V: Bauteil1.5V, Bauteil2.VCC
  N15: Bauteil1.VIN, BAT1.V+, R2.Pin_0

custom parts:
  LCD1602-I2C: A standard character display, usually with 2x16 characters. Comes in many colors with LCM1602 IIC attached.
